# Fritzing sketch Ecosystems (saved by Fritzing 0.9.0b)

parts:
  Part2 = Arduino Ethernet Shield (Rev3)  # not connected
  Part3 = Real Time Clock Module - DS1307 RTC Breakout Board
  Part5 = Arduino Mega 2560 (Rev3)
  Part6 = Arduino Prototyping Shield
  R4 = PHOTOCELL [package=photocell]
  DS2 = DS18B20 1-Wire Temperature Sensor [part_number=DS18B20]
  R5 = Resistor [tolerance=±5% resistance=10k package=THT]
  Part8 = Humidity Sensor - HIH-4030 Breakout

nets:
  5V: Part3.5V, Part6.+5V, Part6.N$239, Part6.N$262, Part6.N$267, Part6.N$355, Part6.N$360, Part6.N$395, R4.P$1, DS2.VDD, Part8.VCC
  GND: Part3.GND, Part6.GND, Part6.N$57, Part6.N$304, Part6.N$305, Part6.N$363, DS2.GND, R5.Pin_0, Part8.GND
  N1: Part3.SCL, Part5.D21/SCL
  N2: Part3.SDA, Part5.D20/SDA
  N3: Part6.D2, Part8.OUT
  N4: Part6.D7, Part6.N$269, DS2.DQ
  N5: Part6.A0, Part6.N$297, Part6.N$317, R4.P$2, R5.Pin_1
